// Logisim project Regfile.circ as structural Verilog: 1 circuit, main circuit main
module main (
  input  [1:0] Read_register_1,
  input  [1:0] Read_register_2,
  input  [1:0] write_register,
  input  [15:0] write_data,
  input  RegWrite,
  input  clock,
  output [15:0] Reg_0_Value,
  output [15:0] Reg_1_Value,
  output [15:0] Reg_2_Value,
  output [15:0] Reg_3_Value,
  output [15:0] Read_Data_1,
  output [15:0] Read_Data_2
);

  wire [15:0] Reg0, Reg1, Reg2, Reg3;

  Register #(.width(16)) register_1 (.D(Reg0), .Q(Reg_0_Value), .clk(clock));  // open: en, clr
  Multiplexer #(.select(2), .width(16)) multiplexer_1 (
    .in0(Reg_0_Value), .in1(Reg_1_Value), .in2(Reg_2_Value), .in3(Reg_3_Value), .out(Read_Data_1),
    .sel(Read_register_1));  // open: en
  Multiplexer #(.select(2), .width(16)) multiplexer_2 (
    .in0(write_data), .in1(Reg_0_Value), .in2(Reg_0_Value), .in3(Reg_0_Value), .out(Reg0),
    .sel(write_register), .en(RegWrite));
  Register #(.width(16)) register_2 (.D(Reg1), .Q(Reg_1_Value), .clk(clock));  // open: en, clr
  Multiplexer #(.select(2), .width(16)) multiplexer_3 (
    .in0(Reg_1_Value), .in1(write_data), .in2(Reg_1_Value), .in3(Reg_1_Value), .out(Reg1),
    .sel(write_register), .en(RegWrite));
  Multiplexer #(.select(2), .width(16)) multiplexer_4 (
    .in0(Reg_2_Value), .in1(Reg_2_Value), .in2(write_data), .in3(Reg_2_Value), .out(Reg2),
    .sel(write_register), .en(RegWrite));
  Register #(.width(16)) register_3 (.D(Reg2), .Q(Reg_2_Value), .clk(clock));  // open: en, clr
  Multiplexer #(.select(2), .width(16)) multiplexer_5 (
    .in0(Reg_0_Value), .in1(Reg_1_Value), .in2(Reg_2_Value), .in3(Reg_3_Value), .out(Read_Data_2),
    .sel(Read_register_2));  // open: en
  Register #(.width(16)) register_4 (.D(Reg3), .Q(Reg_3_Value), .clk(clock));  // open: en, clr
  Multiplexer #(.select(2), .width(16)) multiplexer_6 (
    .in0(Reg_3_Value), .in1(Reg_3_Value), .in2(Reg_3_Value), .in3(write_data), .out(Reg3),
    .sel(write_register), .en(RegWrite));

  // Other names for the same wires on the sheet: Clk = clock; R0[15:0] = Reg_0_Value; R1[15:0] = Reg_1_Value;
  //   R2[15:0] = Reg_2_Value; R3[15:0] = Reg_3_Value; Read1[1:0] = Read_register_1; Read2[1:0] = Read_register_2;
  //   RW = RegWrite; WD[15:0] = write_data; WR[1:0] = write_register

  // Notes on the sheet:
  //   These are INPUTS to the circuit
  //   These are INPUTS to the circuit
  //   DO NOT CHANGE THE LOCATIONS OF THE INPUTS/OUTPUTS! IF YOU DO SO, YOU NEED TO MAKE SURE THE PINS ARE AT THE RIGHT PLACE!
  //   These are OUTPUTS to the circuit
  //   Yet again, the clock is not an actual clock, but an input, one that will should/will be inputed from the higher circuit
  //   These are OUTPUTS to the circuit
endmodule
