// Logisim project alu.circ as structural Verilog: 2 circuits, main circuit main
module main (
  input  [15:0] X,
  input  [15:0] Y,
  input  [3:0] switch__S,
  output signed_overflow,
  output [15:0] result,
  output equal
);

  wire and_2_out, and_3_out, and_4_out, and_5_out, and_6_out, comparator_1_lt, comparator_2_gt,
       comparator_3_lt, comparator_4_gt, comparator_4_lt, comparator_5_eq, comparator_6_eq, comparator_7_eq,
       comparator_8_eq, comparator_9_eq, comparator_10_eq, not_1_out, not_2_out, not_3_out, or_2_out,
       or_3_out;
  wire [1:0] adder_2_out, adder_3_out, adder_4_out, adder_5_out, adder_6_out, adder_7_out, adder_8_out,
       adder_9_out, adder_10_out, adder_11_out, adder_12_out, adder_13_out;
  wire [2:0] adder_14_out, adder_15_out;
  wire [2:2] adder_10_cout, adder_11_cout, adder_12_cout, adder_13_cout;
  wire [3:0] adder_16_out, bit_extender_1_out, bit_extender_2_out, bit_extender_3_out;
  wire [3:3] adder_14_cout, adder_15_cout;
  wire [4:4] adder_16_cout;
  wire [15:0] adder_1_out, and_1_out, bc, bit_extender_4_out, ffo, lui, or_1_out, shifter_2_out,
       shifter_3_out, shifter_4_out, subtractor_1_out, zb;

  assign and_1_out = X & Y;  // AND_Gate and_1, 16 bits wide
  assign or_1_out = X | Y;  // OR_Gate or_1, 16 bits wide
  Comparator #(.width(16)) comparator_1 (.a(X), .b(Y), .eq(equal), .lt(comparator_1_lt));  // open: gt
  Bit_Extender #(.in_width(16), .out_width(4)) bit_extender_1 (.in(Y), .out(bit_extender_1_out));
  Bit_Extender #(.in_width(16), .out_width(4)) bit_extender_2 (.in(Y), .out(bit_extender_2_out));
  Bit_Extender #(.in_width(16), .out_width(4)) bit_extender_3 (.in(Y), .out(bit_extender_3_out));
  Adder #(.width(16)) adder_1 (.a(X), .b(Y), .out(adder_1_out));  // open: cin, cout
  Subtractor #(.width(16)) subtractor_1 (.a(X), .b(Y), .out(subtractor_1_out));  // open: bin, bout
  Comparator #(.width(16)) comparator_2 (.a(X), .b({16{1'b0}}), .gt(comparator_2_gt));  // open: eq, lt
  Comparator #(.width(16)) comparator_3 (.a(Y), .b({16{1'b0}}), .lt(comparator_3_lt));  // open: gt, eq
  ffo ffo_1 (.X(Y), .out(ffo));
  Shifter #(.width(16)) shifter_1 (.in(Y), .\dist (4'b1000), .out(lui));
  assign bit_extender_4_out = {{15{1'b0}}, comparator_1_lt};  // Bit_Extender bit_extender_4
  Shifter #(.width(16)) shifter_2 (.in(X), .\dist (bit_extender_1_out), .out(shifter_2_out));
  Shifter #(.width(16), .shift("lr")) shifter_3 (.in(X), .\dist (bit_extender_2_out), .out(shifter_3_out));
  Shifter #(.width(16), .shift("ar")) shifter_4 (.in(X), .\dist (bit_extender_3_out), .out(shifter_4_out));
  not not_1 (not_1_out, comparator_2_gt);
  not not_2 (not_2_out, adder_1_out[15]);
  Comparator #(.width(16)) comparator_4 (
    .a(subtractor_1_out), .b({16{1'b0}}), .gt(comparator_4_gt), .lt(comparator_4_lt));  // open: eq
  not not_3 (not_3_out, comparator_3_lt);
  Comparator comparator_5 (.a(X[7:0]), .b({8{1'b0}}), .eq(comparator_5_eq));  // open: gt, lt
  Comparator comparator_6 (.a({8{1'b0}}), .b(X[15:8]), .eq(comparator_6_eq));  // open: gt, lt
  and and_2 (and_2_out, comparator_4_lt, comparator_2_gt, comparator_3_lt);
  and and_3 (and_3_out, not_1_out, not_3_out, comparator_4_gt);
  or or_2 (or_2_out, comparator_5_eq, comparator_6_eq);
  Adder #(.width(1)) adder_2 (.a(X[0]), .b(X[1]), .out(adder_2_out[0]), .cout(adder_2_out[1]));  // open: cin
  Adder #(.width(1)) adder_3 (.a(X[2]), .b(X[3]), .out(adder_3_out[0]), .cout(adder_3_out[1]));  // open: cin
  Adder #(.width(1)) adder_4 (.a(X[4]), .b(X[5]), .out(adder_4_out[0]), .cout(adder_4_out[1]));  // open: cin
  Adder #(.width(1)) adder_5 (.a(X[6]), .b(X[7]), .out(adder_5_out[0]), .cout(adder_5_out[1]));  // open: cin
  Adder #(.width(1)) adder_6 (.a(X[8]), .b(X[9]), .out(adder_6_out[0]), .cout(adder_6_out[1]));  // open: cin
  Adder #(.width(1)) adder_7 (.a(X[10]), .b(X[11]), .out(adder_7_out[0]), .cout(adder_7_out[1]));  // open: cin
  Adder #(.width(1)) adder_8 (.a(X[12]), .b(X[13]), .out(adder_8_out[0]), .cout(adder_8_out[1]));  // open: cin
  Adder #(.width(1)) adder_9 (.a(X[14]), .b(X[15]), .out(adder_9_out[0]), .cout(adder_9_out[1]));  // open: cin
  Multiplexer #(.select(4), .width(16)) multiplexer_1 (
    .in0(and_1_out), .in1(or_1_out), .in2(bit_extender_4_out), .in3(shifter_2_out), .in4(shifter_3_out),
    .in5(shifter_4_out), .in6(adder_1_out), .in7(subtractor_1_out), .in8(ffo), .in9(zb), .in10(bc),
    .in11(lui), .out(result), .sel(switch__S));  // open: in12, in13, in14, in15, en
  Comparator #(.width(1)) comparator_7 (.a(X[15]), .b(not_2_out), .eq(comparator_7_eq));  // open: gt, lt
  Comparator #(.width(1)) comparator_8 (.a(not_2_out), .b(Y[15]), .eq(comparator_8_eq));  // open: gt, lt
  or or_3 (or_3_out, and_2_out, and_3_out);
  assign zb = {{15{1'b0}}, or_2_out};  // Bit_Extender bit_extender_5
  Adder #(.width(2)) adder_10 (
    .a(adder_2_out), .b(adder_3_out), .out(adder_10_out), .cout(adder_10_cout[2]));  // open: cin
  Adder #(.width(2)) adder_11 (
    .a(adder_4_out), .b(adder_5_out), .out(adder_11_out), .cout(adder_11_cout[2]));  // open: cin
  Adder #(.width(2)) adder_12 (
    .a(adder_6_out), .b(adder_7_out), .out(adder_12_out), .cout(adder_12_cout[2]));  // open: cin
  Adder #(.width(2)) adder_13 (
    .a(adder_8_out), .b(adder_9_out), .out(adder_13_out), .cout(adder_13_cout[2]));  // open: cin
  and and_4 (and_4_out, comparator_7_eq, comparator_8_eq);
  Comparator #(.width(4)) comparator_9 (.a(4'b0110), .b(switch__S), .eq(comparator_9_eq));  // open: gt, lt
  Comparator #(.width(4)) comparator_10 (.a(switch__S), .b(4'b0111), .eq(comparator_10_eq));  // open: gt, lt
  and and_5 (and_5_out, comparator_10_eq, or_3_out);
  and and_6 (and_6_out, and_4_out, comparator_9_eq);
  Adder #(.width(3)) adder_14 (
    .a({adder_10_cout[2], adder_10_out}), .b({adder_11_cout[2], adder_11_out}), .out(adder_14_out),
    .cout(adder_14_cout[3]));  // open: cin
  Adder #(.width(3)) adder_15 (
    .a({adder_12_cout[2], adder_12_out}), .b({adder_13_cout[2], adder_13_out}), .out(adder_15_out),
    .cout(adder_15_cout[3]));  // open: cin
  buf or_4 (signed_overflow, and_5_out);  // OR_Gate
  Adder #(.width(4)) adder_16 (
    .a({adder_14_cout[3], adder_14_out}), .b({adder_15_cout[3], adder_15_out}), .out(adder_16_out),
    .cout(adder_16_cout[4]));  // open: cin
  assign bc = {{11{1'b0}}, {adder_16_cout[4], adder_16_out}};  // Bit_Extender bit_extender_6

  // Other names for the same wires on the sheet: S[3:0] = switch__S; tunnel = equal

  // Notes on the sheet:
  //   These are INPUTS to your circuit
  //   This is an INPUT to your circuit
  //   DO NOT CHANGE THE LOCATIONS OF THE INPUTS/OUTPUTS! IF YOU DO SO, YOU NEED TO MAKE SURE THE PINS ARE AT THE RIGHT PLACE!
  //   These are OUTPUTS to your circuit
endmodule

module ffo (
  input  [15:0] X,
  output [15:0] out
);

  wire bitfinder_1_found;
  wire [3:0] bitfinder_1_index;
  wire [15:0] bit_extender_1_out, subtractor_1_out;

  // Probe on X
  // Probe on bitfinder_1_index
  assign bit_extender_1_out = {{12{1'b0}}, bitfinder_1_index};  // Bit_Extender bit_extender_1
  BitFinder #(.width(16), .\type ("high1")) bitfinder_1 (.in(X), .index(bitfinder_1_index), .found(bitfinder_1_found));
  Subtractor #(.width(16)) subtractor_1 (.a(16'hf), .b(bit_extender_1_out), .out(subtractor_1_out));  // open: bin, bout
  Multiplexer #(.width(16)) multiplexer_1 (
    .in0(16'h10), .in1(subtractor_1_out), .out(out), .sel(bitfinder_1_found));  // open: en
endmodule
