// Logisim project cpu.circ as structural Verilog: 2 circuits, main circuit main
module main (
  input  [15:0] From_Instr_Mem,
  input  clk,
  output [15:0] r0,
  output [15:0] r1,
  output [15:0] r2,
  output [15:0] r3,
  output [15:0] Display_0,
  output [15:0] Display_1,
  output [15:0] To_Instr_Mem,
  output [15:0] Data_Mem_Data,
  output [15:0] Data_Mem_Addr,
  output Data_Mem_Write
);

  wire and_2_out, and_3_out, bit_extender_3_out, comparator_1_eq, comparator_3_eq, comparator_4_eq,
       comparator_5_eq, comparator_6_eq, comparator_7_eq, comparator_8_eq, disp, Kill,
       main_2_signed_overflow, MemtoReg, multiplexer_3_out, not_1_out, not_2_out, or_2_out, RegW, undriven,
       Zero;
  wire [1:0] regdst;
  wire [3:0] bit_extender_2_out, opcode, S;
  wire [5:0] func;
  wire [7:6] Imm;
  wire [11:8] jaddr;
  wire [15:0] adder_1_out, and_1_out, bit_extender_1_out, bit_extender_4_out, bit_extender_5_out, currPC,
       datamemory_1_data_out, demultiplexer_1_out0, demultiplexer_1_out1, Imm16, multiplexer_1_out,
       multiplexer_2_out, multiplexer_10_out, multiplexer_11_out, multiplexer_14_out, multiplexer_15_out,
       multiplexer_16_out, nPC, or_1_out, PC_1, register_2_q, rsval;

  // Probe on nPC
  Register #(.width(16)) u_currPC (.D(nPC), .Q(currPC), .clk(clk));  // open: en, clr
  Adder #(.width(16)) adder_1 (.a(currPC), .b(Imm16), .out(adder_1_out));  // open: cin, cout
  Register #(.width(16)) register_1 (.D(nPC), .Q(To_Instr_Mem), .clk(clk));  // open: en, clr
  // Probe on opcode
  assign bit_extender_1_out = {{4{1'b0}}, {jaddr, Imm, func}};  // Bit_Extender bit_extender_1
  Multiplexer #(.width(16)) multiplexer_1 (
    .in0(PC_1), .in1(adder_1_out), .out(multiplexer_1_out), .sel(Zero));  // open: en
  Multiplexer #(.width(16)) multiplexer_2 (
    .in0(adder_1_out), .in1(PC_1), .out(multiplexer_2_out), .sel(Zero));  // open: en
  Register #(.width(16)) register_2 (.D(From_Instr_Mem), .Q(register_2_q), .clk(clk));  // open: en, clr
  Register #(.width(1)) u_Kill (.D(multiplexer_3_out), .Q(Kill), .clk(clk));  // open: en, clr
  Multiplexer #(.select(4)) multiplexer_3 (
    .in0(1'b0), .in1(1'b0), .in2(1'b0), .in3(1'b0), .in4(1'b0), .in5(1'b0), .in6(1'b0), .in7(1'b1),
    .in8(1'b1), .in9(1'b1), .in10(Zero), .in11(not_1_out), .in12(1'b0), .in13(1'b0), .in14(1'b0),
    .in15(1'b0), .out(multiplexer_3_out), .sel(opcode));  // open: en
  Adder #(.width(16)) adder_2 (.a(16'h1), .b(currPC), .out(PC_1));  // open: cin, cout
  assign and_1_out = currPC & 16'hf000;  // AND_Gate and_1, 16 bits wide
  Multiplexer #(.width(16)) multiplexer_4 (
    .in0(register_2_q), .in1({16{1'b0}}), .out({opcode, jaddr, Imm, func}), .sel(Kill));  // open: en
  not not_1 (not_1_out, Zero);
  assign or_1_out = bit_extender_1_out | and_1_out;  // OR_Gate or_1, 16 bits wide
  Comparator #(.width(4)) comparator_1 (.a(opcode), .b(4'b1110), .eq(comparator_1_eq));  // open: gt, lt
  Multiplexer #(.select(4), .width(16)) multiplexer_5 (
    .in0(PC_1), .in1(PC_1), .in2(PC_1), .in3(PC_1), .in4(PC_1), .in5(PC_1), .in6(PC_1), .in7(or_1_out),
    .in8(or_1_out), .in9(rsval), .in10(multiplexer_1_out), .in11(multiplexer_2_out), .in12(PC_1),
    .in13(PC_1), .in14(PC_1), .in15(PC_1), .out(nPC), .sel(opcode));  // open: en
  // Probe on opcode
  Bit_Extender #(.in_width(6), .out_width(4)) bit_extender_2 (.in(func), .out(bit_extender_2_out));
  Multiplexer multiplexer_6 (.in0(1'b0), .in1(1'b1), .out(MemtoReg), .sel(comparator_1_eq));  // open: en
  Comparator #(.width(4)) comparator_2 (.a(4'b1111), .b(opcode), .eq(disp));  // open: gt, lt
  // Probe on nPC
  Comparator #(.width(4)) comparator_3 (.a(opcode), .b(4'b0111), .eq(comparator_3_eq));  // open: gt, lt
  Multiplexer #(.select(4), .width(2)) multiplexer_7 (
    .in0(Imm), .in1(jaddr[9:8]), .in2(jaddr[9:8]), .in3(jaddr[9:8]), .in4(jaddr[9:8]), .in5(jaddr[9:8]),
    .in6(jaddr[9:8]), .in7(2'b11), .in8(2'b00), .in9(2'b00), .in10(2'b00), .in11(2'b00), .in12(jaddr[9:8]),
    .in13(jaddr[9:8]), .in14(jaddr[9:8]), .out(regdst), .sel(opcode));  // open: in15, en
  // Probe on S
  Multiplexer #(.select(4), .width(4)) multiplexer_8 (
    .in0(bit_extender_2_out), .in1(4'b1000), .in2(4'b1001), .in3(4'b1010), .in4(4'b0110), .in5(4'b0000),
    .in6(4'b0001), .in12(4'b0110), .in13(4'b1011), .in14(4'b0110), .out(S), .sel(opcode));  // open: in7, in8, in9, in10, in11, in15, en
  // Probe on multiplexer_10_out
  Multiplexer #(.select(4)) multiplexer_9 (
    .in0(1'b1), .in1(1'b1), .in2(1'b1), .in3(1'b1), .in4(1'b1), .in5(1'b1), .in6(1'b1), .in7(1'b1),
    .in8(1'b0), .in9(1'b0), .in10(1'b0), .in11(1'b0), .in12(1'b0), .in13(1'b1), .in14(1'b1), .in15(1'b0),
    .out(RegW), .sel(opcode));  // open: en
  Bit_Extender #(.out_width(1)) bit_extender_3 (.in({Imm, func}), .out(bit_extender_3_out));
  Multiplexer #(.width(16)) multiplexer_10 (
    .in0(multiplexer_15_out), .in1(currPC), .out(multiplexer_10_out), .sel(comparator_3_eq));  // open: en
  Regfile_main main_1 (
    .Read_register_1(jaddr[11:10]), .Read_register_2(jaddr[9:8]), .write_register(regdst),
    .write_data(multiplexer_10_out), .Reg_0_Value(r0), .Reg_1_Value(r1), .Reg_2_Value(r2), .Reg_3_Value(r3),
    .RegWrite(RegW), .clock(clk), .Read_Data_1(rsval), .Read_Data_2(Data_Mem_Data));
  assign bit_extender_4_out = {{8{1'b0}}, {Imm, func}};  // Bit_Extender bit_extender_4
  assign bit_extender_5_out = {{8{Imm[7]}}, {Imm, func}};  // Bit_Extender bit_extender_5
  Multiplexer #(.width(16)) multiplexer_11 (
    .in0(Display_0), .in1(Display_1), .out(multiplexer_11_out), .sel(bit_extender_3_out));  // open: en
  Comparator #(.width(1)) comparator_4 (.a(bit_extender_3_out), .b(1'b0), .eq(comparator_4_eq));  // open: gt, lt
  Comparator #(.width(1)) comparator_5 (.a(bit_extender_3_out), .b(1'b1), .eq(comparator_5_eq));  // open: gt, lt
  // Probe on rsval
  Multiplexer #(.select(4), .width(16)) multiplexer_12 (
    .in0(bit_extender_4_out), .in1(bit_extender_4_out), .in2(bit_extender_4_out), .in3(bit_extender_4_out),
    .in4(bit_extender_5_out), .in5(bit_extender_4_out), .in6(bit_extender_4_out), .in7(bit_extender_4_out),
    .in8(bit_extender_4_out), .in9(bit_extender_4_out), .in10(bit_extender_5_out), .in11(bit_extender_5_out),
    .in12(bit_extender_5_out), .in13(bit_extender_4_out), .in14(bit_extender_5_out),
    .in15(bit_extender_4_out), .out(Imm16), .sel(opcode));  // open: en
  Multiplexer #(.select(4)) multiplexer_13 (
    .in0(1'b0), .in1(1'b0), .in2(1'b0), .in3(1'b0), .in4(1'b0), .in5(1'b0), .in6(1'b0), .in7(1'b0),
    .in8(1'b0), .in9(1'b0), .in10(1'b0), .in11(1'b0), .in12(1'b1), .in13(1'b0), .in14(1'b0), .in15(1'b0),
    .out(Data_Mem_Write), .sel(opcode));  // open: en
  Multiplexer #(.width(16)) multiplexer_14 (
    .in0(multiplexer_11_out), .in1(rsval), .out(multiplexer_14_out), .sel(disp));  // open: en
  Multiplexer #(.width(16)) multiplexer_15 (
    .in0(Data_Mem_Addr), .in1(datamemory_1_data_out), .out(multiplexer_15_out), .sel(MemtoReg));  // open: en
  Multiplexer #(.width(16)) multiplexer_16 (
    .in0(Data_Mem_Data), .in1(Imm16), .out(multiplexer_16_out), .sel(not_2_out));  // open: en
  Comparator #(.width(4)) comparator_6 (.a(4'b0000), .b(opcode), .eq(comparator_6_eq));  // open: gt, lt
  Comparator #(.width(4)) comparator_7 (.a(opcode), .b(4'b1010), .eq(comparator_7_eq));  // open: gt, lt
  Comparator #(.width(4)) comparator_8 (.a(opcode), .b(4'b1011), .eq(comparator_8_eq));  // open: gt, lt
  // Probe on Imm16
  Hex_Digit_Display hex_digit_display_1 (.value(Display_0[11:8]));  // open: dp
  Hex_Digit_Display hex_digit_display_2 (.value(Display_0[15:12]));  // open: dp
  Register #(.width(16)) d0 (.D(demultiplexer_1_out0), .en(and_2_out), .Q(Display_0), .clk(clk), .clr(undriven));
  Demultiplexer #(.width(16), .enable("false")) demultiplexer_1 (
    .out0(demultiplexer_1_out0), .out1(demultiplexer_1_out1), .in(multiplexer_14_out),
    .sel(bit_extender_3_out));
  DotMatrix #(.matrixcols(1), .matrixrows(1)) dotmatrix_1 (.col0(main_2_signed_overflow));
  // Probe on Data_Mem_Addr
  // Probe on Data_Mem_Addr
  alu_main main_2 (
    .switch__S(S), .X(rsval), .equal(Zero), .result(Data_Mem_Addr), .signed_overflow(main_2_signed_overflow),
    .Y(multiplexer_16_out));
  not not_2 (not_2_out, or_2_out);
  or or_2 (or_2_out, comparator_6_eq, comparator_7_eq, comparator_8_eq);
  Hex_Digit_Display hex_digit_display_3 (.value(Display_0[3:0]));  // open: dp
  Hex_Digit_Display hex_digit_display_4 (.value(Display_0[7:4]));  // open: dp
  and and_2 (and_2_out, comparator_4_eq, disp);
  // Probe on Data_Mem_Data
  datamemory datamemory_1 (
    .DataIn(Data_Mem_Data), .Address(Data_Mem_Addr), .Data_out(datamemory_1_data_out),
    .MemWrite(Data_Mem_Write));  // open: Reset
  Hex_Digit_Display hex_digit_display_5 (.value(Display_1[11:8]));  // open: dp
  Hex_Digit_Display hex_digit_display_6 (.value(Display_1[15:12]));  // open: dp
  Register #(.width(16)) d1 (.D(demultiplexer_1_out1), .en(and_3_out), .Q(Display_1), .clk(clk));  // open: clr
  and and_3 (and_3_out, disp, comparator_5_eq);
  // Probe on datamemory_1_data_out
  Hex_Digit_Display hex_digit_display_7 (.value(Display_1[3:0]));  // open: dp
  Hex_Digit_Display hex_digit_display_8 (.value(Display_1[7:4]));  // open: dp

  // Other names for the same wires on the sheet: Imm[5:0] = func; jaddr[7:0] = {Imm, func}; rd[1:0] = Imm;
  //   rt[1:0] = jaddr[9:8]; rs[1:0] = jaddr[11:10]; d0[15:0] = Display_0; d1[15:0] = Display_1;
  //   MemWrite = Data_Mem_Write

  // Notes on the sheet:
  //   This is the instruction that you would receive as INPUT
  //   This is the current PC that you need to send as OUTPUT
  //   This is a CLK that is an INPUT driven from the harness.
  //   Remember, this circuit is loaded from the harness to be tested!
  //   DO NOT CHANGE THE LOCATIONS OF THE INPUTS/OUTPUTS! IF YOU DO SO, YOU NEED TO MAKE SURE THE PINS ARE AT THE RIGHT PLACE!
  //   These are OUTPUTS to the circuit
  //   These are OUTPUTS to the circuit
endmodule

// Mem
module datamemory (
  input  [15:0] DataIn,
  input  [15:0] Address,
  input  Reset,
  input  MemWrite,
  output [15:0] Data_out
);

  wire clock_1_out, not_1_out;

  assign Data_out = MemWrite ? DataIn : 16'bz;  // Controlled_Buffer controlled_buffer_1
  Clock clock_1 (.out(clock_1_out));
  RAM #(.addrWidth(16), .dataWidth(16)) ram_1 (
    .addr(Address), .data(Data_out), .sel(1'b1), .clk(clock_1_out), .ld(not_1_out), .clr(Reset));
  not not_1 (not_1_out, MemWrite);
endmodule
